# Fritzing sketch Arduino Domótica Jhovy (saved by Fritzing 0.9.3b)

parts:
  Ethernet_SHIELD = Arduino Mega 2560 (Rev3)
  Arduino_MEGA = Arduino Ethernet Shield (Rev3)
  Sensor_PIR = HC-SR501 Body Sensor Module
  Nano_Arduino = Arduino Nano (Rev3.0)
  Relay = Jtron 1 Channel Optoisolated Relay Module [package=relay]
  4_Module_Relay = 4 Channel Power Relay
  Fotoresistencia_ARD-LDR = LM393 LDR breakout [part_number=100027]

nets:
  N1: Ethernet_SHIELD.D22, 4_Module_Relay.IN1
  N2: Ethernet_SHIELD.D23, 4_Module_Relay.IN2
  N3: Ethernet_SHIELD.D24, 4_Module_Relay.IN3
  N4: Ethernet_SHIELD.D25, 4_Module_Relay.IN4
  GND: Ethernet_SHIELD.GND, Fotoresistencia_ARD-LDR.GND
  GND_2: Arduino_MEGA.GND, 4_Module_Relay.GND
  N5: Arduino_MEGA.A0, Fotoresistencia_ARD-LDR.AO
  VCC: Arduino_MEGA.5V, 4_Module_Relay.VCC, Fotoresistencia_ARD-LDR.VCC
  VCC_2: Sensor_PIR.VCC, Nano_Arduino.5V, Relay.VCC
  N6: Sensor_PIR.OUT, Nano_Arduino.D2
  GND_3: Sensor_PIR.GND, Nano_Arduino.GND, Relay.GND
  N7: Nano_Arduino.D3, Relay.IN1

custom parts:
  HC-SR501 Body Sensor Module: Pyroelectric Infrared PIR Motion Sensor Detector Module
  4 Channel Power Relay: A 4 channel power relay. The module operates at 5V.
